# Fritzing sketch clock (saved by Fritzing 0.9.4)
breadboards: 2

parts:
  Part1 = Arduino Uno (Rev3)
  U1 = 74HC595 [package="DIP16 [THT]"]
  U2 = 74HC595 [package="DIP16 [THT]"]
  R1 = Resistor [tolerance=±5% resistance=150 package=THT]
  R2 = Resistor [tolerance=±5% resistance=150 package=THT]
  R3 = Resistor [tolerance=±5% resistance=150 package=THT]
  R4 = Resistor [tolerance=±5% resistance=150 package=THT]
  R5 = Resistor [tolerance=±5% resistance=150 package=THT]
  R6 = Resistor [tolerance=±5% resistance=150 package=THT]
  R7 = Resistor [tolerance=±5% resistance=150 package=THT]
  R8 = Resistor [tolerance=±5% resistance=150 package=THT]
  Q1 = NPN-Transistor [package="TO92 [THT]"]
  Q2 = NPN-Transistor [package="TO92 [THT]"]
  Q3 = NPN-Transistor [package="TO92 [THT]"]
  Q4 = NPN-Transistor [package="TO92 [THT]"]
  R9 = Resistor [tolerance=±5% resistance=2.2k package=THT]
  R10 = Resistor [tolerance=±5% resistance=2.2k package=THT]
  R11 = Resistor [tolerance=±5% resistance=2.2k package=THT]
  R12 = Resistor [tolerance=±5% resistance=2.2k package=THT]
  LED1 = 7-SEGMENT-4DIGIT-YOUNGSUN [package=7-segment-4digit-youngsun]

nets:
  N1: Part1.D2, U1.DS
  VCC: Part1.D3_PWM, U1.MR, U1.SH_CP, U1.VCC, U2.SH_CP, U2.VCC, R8.Pin_0
  N2: Part1.D4, U1.ST_CP, U2.ST_CP
  N3: U1.Q1, R4.Pin_0
  N4: U1.Q2, R2.Pin_0
  N5: U1.Q3, R3.Pin_0
  N6: U1.Q4, R5.Pin_0
  N7: U1.Q5, R6.Pin_0
  N8: U1.Q6, R7.Pin_0
  GND: U1.GND, U2.GND, LED1.DP
  N9: U1.Q7', U2.DS
  N10: U1.OE, U2.OE
  N11: U1.Q0, R1.Pin_0
  N12: R1.Pin_1, LED1.A
  N13: R2.Pin_1, LED1.C
  N14: R6.Pin_1, LED1.F
  N15: R8.Pin_1, LED1.APOS-A
  N16: Q1.B, R9.Pin_0
  N17: Q2.B, R10.Pin_0
  N18: Q3.B, R11.Pin_0
  N19: Q3.C, LED1.COL-C
  N20: Q4.B, R12.Pin_0
  N21: Q4.C, LED1.DIG3
