# Fritzing sketch clock1 (saved by Fritzing 0.9.4)
circuit board: 8.46667cm x 5.64444cm
perfboards: 1

parts:
  U2 = 74HC595 SMD [package="SO16 [SMD]"]
  U3 = 7-SEGMENT-4DIGIT [package=7-segment-4digit-youngsun]
  R8 = Resistor [tolerance=±5% resistance=150 package=THT]
  R9 = Resistor [tolerance=±5% resistance=150 package=THT]
  R10 = Resistor [tolerance=±5% resistance=150 package=THT]
  R11 = Resistor [tolerance=±5% resistance=150 package=THT]
  R12 = Resistor [tolerance=±5% resistance=150 package=THT]
  R13 = Resistor [tolerance=±5% resistance=150 package=THT]
  R14 = Resistor [tolerance=±5% resistance=150 package=THT]
  U4 = 74HC595 SMD [package="SO16 [SMD]"]
  Part1 = Arduino Nano (Rev3.0)
  J1 = Power Jack [package=power_jack_smd]
  R7 = Resistor [tolerance=±5% resistance=150 package=THT]
  Q1 = NPN-Transistor [package="TO92 [THT]"]
  Q2 = NPN-Transistor [package="TO92 [THT]"]
  Q3 = NPN-Transistor [package="TO92 [THT]"]
  Q4 = NPN-Transistor [package="TO92 [THT]"]

nets:
  N1: U2.Q1, R7.Pin_0
  N2: U2.Q2, R8.Pin_0
  N3: U2.Q3, R9.Pin_0
  N4: U2.Q4, R10.Pin_0
  N5: U2.Q5, R11.Pin_0
  N6: U2.Q6, R12.Pin_0
  N7: U2.Q7, R13.Pin_0
  GND: U2.GND, U2.MR, Part1.GND, J1.GND, Q4.E
  N8: U2.Q7', U4.DS
  N9: U2.SH_CP, U4.SH_CP, Part1.D4
  N10: U2.ST_CP, U4.ST_CP, Part1.D3
  VCC: U2.OE, U2.VCC, U4.OE, U4.VCC, Part1.5V
  N11: U2.DS, Part1.D2
  N12: U2.Q0, R14.Pin_0
  N13: U3.1, R10.Pin_1
  N14: U3.2, R11.Pin_1
  N15: U3.4, R12.Pin_1
  N16: U3.5, R8.Pin_1
  N17: U3.9, R7.Pin_1
  N18: U3.10, R13.Pin_1
  N19: U3.11, Q2.C
  N20: U3.12, R9.Pin_1
  N21: U3.13, R14.Pin_1
  N22: U3.14, Q1.C
  N23: U4.Q1, Q2.B
  N24: U4.Q2, Q3.B
  N25: U4.Q3, Q4.B
  N26: U4.Q0, Q1.B
  N27: Part1.VIN, J1.PWR
