# Fritzing sketch hygrometer (saved by Fritzing 0.8.7b)
breadboards: 1

parts:
  Part1 = Arduino Uno (Rev3)
  R8 = Resistor [tolerance=±5% resistance=220 package=THT]
  LED5 = LED - 5mm [color="Red (660nm)" package="5 mm [THT]"]
  R9 = Resistor [tolerance=±5% resistance=220 package=THT]
  LED6 = LED - 5mm [color="Red (660nm)" package="5 mm [THT]"]
  R10 = Resistor [tolerance=±5% resistance=220 package=THT]
  LED7 = LED - 5mm [color="Red (660nm)" package="5 mm [THT]"]
  R11 = Resistor [tolerance=±5% resistance=220 package=THT]
  LED8 = LED - 5mm [color="Red (660nm)" package="5 mm [THT]"]
  R12 = Resistor [tolerance=±5% resistance=220 package=THT]
  LED9 = LED - 5mm [color="Red (660nm)" package="5 mm [THT]"]
  Part2 = FC-28 Soil Hygrometer Module - Probe
  Part3 = FC-28 Soil Hygrometer Module
  Part4 = FC-28 Soil Hygrometer Module - Probe
  Part5 = FC-28 Soil Hygrometer Module
  Part6 = FC-28 Soil Hygrometer Module - Probe
  Part7 = FC-28 Soil Hygrometer Module
  Part8 = FC-28 Soil Hygrometer Module - Probe
  Part9 = FC-28 Soil Hygrometer Module
  Part10 = FC-28 Soil Hygrometer Module - Probe
  Part11 = FC-28 Soil Hygrometer Module

nets:
  N1: Part1.A0, Part11.AO
  N2: Part1.A1, Part9.AO
  N3: Part1.A2, Part7.AO
  N4: Part1.A3, Part5.AO
  N5: Part1.A4/SDA, Part3.AO
  GND: Part1.GND, LED5.cathode, LED6.cathode, LED8.cathode, LED9.cathode, Part3.GND, Part5.GND, Part7.GND, Part9.GND, Part11.GND
  N6: Part1.D2, R8.Pin_0
  N7: Part1.D3_PWM, R9.Pin_0
  N8: Part1.D4, R10.Pin_0
  N9: Part1.D5_PWM, R11.Pin_0
  N10: Part1.D6_PWM, R12.Pin_0
  VCC: Part1.5V, Part3.VCC, Part7.VCC, Part9.VCC, Part11.VCC
  N11: R8.Pin_1, LED5.anode
  N12: R9.Pin_1, LED6.anode
  N13: R10.Pin_1, LED7.anode
  N14: R11.Pin_1, LED8.anode
  N15: R12.Pin_1, LED9.anode
  N16: Part2.POS, Part3.POS
  N17: Part2.NEG, Part3.NEG
  N18: Part4.POS, Part5.POS
  N19: Part4.NEG, Part5.NEG
  N20: Part6.POS, Part7.POS
  N21: Part6.NEG, Part7.NEG
  N22: Part8.POS, Part9.POS
  N23: Part8.NEG, Part9.NEG
  N24: Part10.POS, Part11.POS
  N25: Part10.NEG, Part11.NEG

custom parts:
  FC-28 Soil Hygrometer Module - Probe: The FC-28 is a soil hygrometer module that uses the Texas Instruments LM393 comparator chip to provide an analog measurement of soil humidity.
  FC-28 Soil Hygrometer Module: The FC-28 is a soil hygrometer module that uses the Texas Instruments LM393 comparator chip to provide an analog measurement of soil humidity. The digital output is high when soil moisture is over a certain threshold, as determined by adjusting the potentiometer.
