# Fritzing sketch simon (saved by Fritzing 0.8.7b)
breadboards: 1

parts:
  Part1 = Arduino Uno (Rev3)
  R1 = Resistor [tolerance=±5% resistance=10k package=THT]
  R2 = Resistor [tolerance=±5% resistance=10k package=THT]
  R3 = Resistor [tolerance=±5% resistance=10k package=THT]
  S1 = Pushbutton [package="[THT]"]
  S2 = Pushbutton [package="[THT]"]
  S3 = Pushbutton [package="[THT]"]
  S4 = Pushbutton [package="[THT]"]
  LED1 = LED - 5mm [color="Blue (430nm)" package="5 mm [THT]"]
  R4 = Resistor [tolerance=±5% resistance=220 package=THT]
  R5 = Resistor [tolerance=±5% resistance=220 package=THT]
  LED2 = LED - 5mm [color="Yellow (585nm)" package="5 mm [THT]"]
  R6 = Resistor [tolerance=±5% resistance=220 package=THT]
  LED3 = LED - 5mm [color="Green (555nm)" package="5 mm [THT]"]
  R7 = Resistor [tolerance=±5% resistance=220 package=THT]
  LED4 = LED - 5mm [color="Red (660nm)" package="5 mm [THT]"]
  R8 = Resistor [tolerance=±5% resistance=10k package=THT]
  J1 = Piezo Speaker
  SW1 = DIP SWITCH [package=dipswitch-02]
  R9 = Resistor [tolerance=±5% resistance=10k package=THT]
  R10 = Resistor [tolerance=±5% resistance=10k package=THT]

nets:
  N1: Part1.D8, S4.Pin_1, S4.Pin_2, R8.Pin_0
  N2: Part1.D9_PWM, R3.Pin_0, S3.Pin_1, S3.Pin_2
  N3: Part1.D10_PWM/SS, R2.Pin_0, S2.Pin_1, S2.Pin_2
  N4: Part1.D11_PWM/MOSI, R1.Pin_0, S1.Pin_1, S1.Pin_2
  N5: Part1.D12/MISO, J1.pin2
  N6: Part1.GND, R1.Pin_1, R2.Pin_1, R3.Pin_1, LED1.cathode, LED2.cathode, LED3.cathode, LED4.cathode, R8.Pin_1, J1.pin1, R9.Pin_1, R10.Pin_1
  N7: Part1.D2, SW1.3, R9.Pin_0
  N8: Part1.D3_PWM, SW1.4, R10.Pin_0
  N9: Part1.D4, R7.Pin_0
  N10: Part1.D5_PWM, R6.Pin_0
  N11: Part1.D6_PWM, R5.Pin_0
  N12: Part1.D7, R4.Pin_0
  N13: Part1.5V, S1.Pin_3, S1.Pin_4, S2.Pin_3, S2.Pin_4, S3.Pin_3, S3.Pin_4, SW1.1, SW1.2
  N14: S4.Pin_3, S4.Pin_4
  N15: LED1.anode, R4.Pin_1
  N16: R5.Pin_1, LED2.anode
  N17: R6.Pin_1, LED3.anode
  N18: R7.Pin_1, LED4.anode
